# Fritzing sketch RPi-Monitor-LCD (saved by Fritzing 0.8.3b)
circuit board: 5.24081cm x 9.67243cm
breadboards: 1

parts:
  S1 = Pushbutton [package="[THT]"]
  S2 = Pushbutton [package="[THT]"]
  S3 = Pushbutton [package="[THT]"]
  S4 = Pushbutton [package="[THT]"]
  S5 = Pushbutton [package="[THT]"]
  MCP23008 = IC, DIP package, 18 pins [chip_label=MCP23008]
  J1 = shrouded pin header, 26 pins [form="♂ (shrouded male)"]
  DS1 = DS18B20 1-Wire Temperature Sensor [part_number=DS18B20]
  R1 = Resistor [tolerance=±5% resistance=4.7k package=THT]
  U1 = mystery part, 3 pins [chip_label=RFe]
  U2 = mystery part, 4 pins [chip_label=RFr]
  J4 = male pin header, 2 pins [form="♂ (male)"]
  J2 = male pin header, 3 pins [form="♂ (male)"]
  IC1 = IC, SIP package, 8 pins [chip_label=PCD8544]
  J6 = male pin header, 8 pins [form="♂ (male)"]
  J7 = male pin header, 8 pins [form="♂ (male)"]

nets:
  N1: S1.Pin_1, S1.Pin_2, MCP23008.pin10
  N2: S1.Pin_3, S1.Pin_4, S2.Pin_3, S2.Pin_4, S3.Pin_3, S3.Pin_4, S4.Pin_3, S4.Pin_4, S5.Pin_3, S5.Pin_4, MCP23008.pin3, MCP23008.pin4, MCP23008.pin5, MCP23008.pin9, J1.pin17, DS1.VDD, R1.Pin_0, U1.pin1, U2.pin1, J4.pin2, IC1.pin7
  N3: S2.Pin_1, S2.Pin_2, MCP23008.pin11
  N4: S3.Pin_1, S3.Pin_2, MCP23008.pin12
  N5: S4.Pin_1, S4.Pin_2, MCP23008.pin13
  N6: S5.Pin_1, S5.Pin_2, MCP23008.pin14
  N7: MCP23008.pin1, J1.pin3
  N8: MCP23008.pin2, J1.pin2
  N9: MCP23008.pin6, MCP23008.pin18, J1.pin1, DS1.GND, R1.Pin_1, U1.pin2, U2.pin4, J4.pin1, IC1.pin8
  N10: MCP23008.pin15, J2.pin3
  N11: MCP23008.pin16, J2.pin2
  N12: MCP23008.pin17, J2.pin1
  N13: J1.pin4, DS1.DQ
  N14: J1.pin6, U1.pin3
  N15: J1.pin7, U2.pin3
  N16: J1.pin10, IC1.pin3
  N17: J1.pin12, IC1.pin2
  N18: J1.pin15, IC1.pin6
  N19: J1.pin18, IC1.pin5
  N20: J1.pin19, IC1.pin4
  N21: J1.pin21, IC1.pin1
  N22: J6.pin1, J7.pin1
  N23: J6.pin2, J7.pin2
  N24: J6.pin3, J7.pin3
  N25: J6.pin4, J7.pin4
  N26: J6.pin5, J7.pin5
  N27: J6.pin6, J7.pin6
  N28: J6.pin7, J7.pin7
  N29: J6.pin8, J7.pin8

notes:
  LCD pin name and connection (from left to right)
  LIGHT GPIO18
  CLK GPIO11 (SCLK)
  DNK GPIO10 (MOSI)
  D/C GPIO23
  RST GPIO24
  SCE GPIO08 (CSO)
  GND GPIO06 (GND)
  VCC GPIO01 (3V3)
  Xavier Berger
  Copyright 2013
  RPI-Monitor-LCD v1.0
  Model B Rev. 2
  RPi-Monitor, RPi-Monitor-LCD for Raspberry Pi Model B rev. 2, 1.0
  For Raspberry Pi
